# Fritzing sketch Timer_Circuit_Bread_Board (saved by Fritzing 0.9.10b)
breadboards: 1

parts:
  LED2 = LED - 5mm [color="Red (633nm)" current=0.030 package="5 mm [THT]"]
  R5 = Resistor [tolerance=±5% power=0.25 resistance=220 package=THT]
  R7 = Resistor [tolerance=±5% power=0.25 resistance=10k package=THT]
  R4 = Resistor [tolerance=±5% power=0.25 resistance=220 package=THT]
  R3 = Resistor [tolerance=±5% power=0.25 resistance=220 package=THT]
  Part1 = Arduino Uno (Rev3)
  LED6 = LED - 5mm [color="Red (633nm)" current=0.030 package="5 mm [THT]"]
  LED1 = LED - 5mm [color="Red (633nm)" current=0.030 package="5 mm [THT]"]
  S1 = Pushbutton [package="[THT]"]
  R1 = Resistor [tolerance=±5% power=0.25 resistance=220 package=THT]
  LED5 = LED - 5mm [color="Red (633nm)" current=0.030 package="5 mm [THT]"]
  LED4 = LED - 5mm [color="Red (633nm)" current=0.030 package="5 mm [THT]"]
  R2 = Resistor [tolerance=±5% power=0.25 resistance=220 package=THT]
  R6 = Resistor [tolerance=±5% power=0.25 resistance=220 package=THT]
  LED3 = LED - 5mm [color="Red (633nm)" current=0.030 package="5 mm [THT]"]

nets:
  N1: LED2.cathode, R7.Pin_1, Part1.GND, LED6.cathode, LED1.cathode, LED5.cathode, LED4.cathode, LED3.cathode
  N2: LED2.anode, R2.Pin_0
  N3: R5.Pin_0, LED3.anode
  N4: R5.Pin_1, Part1.D4
  N5: R7.Pin_0, Part1.D9_PWM, S1.Pin_3, S1.Pin_4
  N6: R4.Pin_0, LED6.anode
  N7: R4.Pin_1, Part1.D7
  N8: R3.Pin_0, LED4.anode
  N9: R3.Pin_1, Part1.D2
  N10: Part1.D3_PWM, R1.Pin_1
  N11: Part1.D5_PWM, R2.Pin_1
  N12: Part1.D6_PWM, R6.Pin_1
  N13: Part1.5V, S1.Pin_1, S1.Pin_2
  N14: LED1.anode, R6.Pin_0
  N15: R1.Pin_0, LED5.anode
